// Logisim project 8 bits architecture.circ as structural Verilog: 1 circuit, main circuit 8 bits architecture
module _8_bits_architecture (
  input  switch_auto_manual,
  input  run_programming_mode_switch,
  input  [3:0] in_3,
  input  [7:0] in_4
);

  wire adder_1_carry_out, ALU_out, ALU_sub, and_1_out, and_2_out, clk, Disp_in, hlt, Instr_reg_in,
       Instr_reg_out, manual_push_button_out, n2_to_1_multiplexer_1_output, not_1_out, not_2_out, not_3_out,
       PC_en, PC_J, PC_JC, PC_out, RAM___in, RAM_in, RAM_out, RAM_progamming_push_button_out, RegA_in,
       RegA_out, RegB_in, system_clock_out;
  wire [3:0] n2to1_4bits_multiplexer_1_output, n4_bits_register_1_output,
       register_8bits_1_uncontrolled_output;
  wire [6:0] Counter_mod_5_output;
  wire [7:0] A, adder_1_sum, ALU_output, B, bus_1_to_leds, Complement_output, Counter_output,
       Decoder_3_to_8_output, Display_input, Inst_reg_output, Instr_reg_input,
       n2to1_8bits_multiplexer_1_output, PC_input, PC_output, RAM, RAM_input, RAM_output,
       RAM_uncontrolled_output_value, RegA_input, RegA_output, RegB_input, RegB_output,
       Register_uncontrolled_output, rom_2_data, rom_3_data, rom_4_data;
  wire [7:4] register_8bits_1_controlled_output;

  LED led_1 (.in(n4_bits_register_1_output[3]));
  Clock system_clock (.out(system_clock_out));
  Button manual_push_button (.out(manual_push_button_out));
  LED led_2 (.in(n4_bits_register_1_output[1]));
  LED led_3 (.in(n4_bits_register_1_output[2]));
  LED led_4 (.in(n4_bits_register_1_output[0]));
  Pull_Resistor pull_resistor_1 (.node(RAM[7]));
  Pull_Resistor pull_resistor_2 (.node(RAM[5]));
  Pull_Resistor pull_resistor_3 (.node(RAM[6]));
  LED led_5 (.in(hlt));
  LED led_6 (.in(RAM___in));
  LED led_7 (.in(switch_auto_manual));
  _4_bits_register u_4_bits_register_1 (
    .\input (RAM[3:0]), .clk(clk), .in(RAM___in), .\output (n4_bits_register_1_output));
  Pull_Resistor pull_resistor_4 (.node(RAM[4]));
  Register_8bits register_8bits_1 (
    .\input (Instr_reg_input), .clk(clk), .in_enable(Instr_reg_in), .out_enable(Instr_reg_out),
    .controlled_output({register_8bits_1_controlled_output, Inst_reg_output[3:0]}),
    .uncontrolled_output({Counter_mod_5_output[6:3], register_8bits_1_uncontrolled_output}));
  LED led_8 (.in(Instr_reg_out));
  LED led_9 (.in(RAM_in));
  LED led_10 (.in(Instr_reg_in));
  LED led_11 (.in(RAM_out));
  LED led_12 (.in(not_1_out));
  not not_1 (not_1_out, switch_auto_manual);
  ROM #(.addrWidth(7), .dataWidth(16)) rom_1 (
    .addr(Counter_mod_5_output),
    .data({PC_JC, PC_J, PC_out, PC_en, Disp_in, RegB_in, ALU_sub, ALU_out, RegA_out, RegA_in, Instr_reg_out, Instr_reg_in, RAM_out, RAM_in, RAM___in, hlt}));  // open: sel
  LED led_13 (.in(ALU_out));
  LED led_14 (.in(RegA_in));
  LED led_15 (.in(RegA_out));
  LED led_16 (.in(ALU_sub));
  LED led_17 (.in(clk));
  Clock Clock (
    .clk(system_clock_out), .switch(switch_auto_manual), .manual(manual_push_button_out), .hlt(hlt),
    .clock_output(clk));
  LED run_mode_on (.in(not_2_out));
  LED programming_mode_on (.in(run_programming_mode_switch));
  LED led_18 (.in(PC_out));
  LED led_19 (.in(PC_en));
  LED led_20 (.in(Disp_in));
  LED led_21 (.in(RegB_in));
  not not_2 (not_2_out, run_programming_mode_switch);
  _2to1_4bits_multiplexer u_2to1_4bits_multiplexer_1 (
    .A(n4_bits_register_1_output), .B(in_3), .selector(run_programming_mode_switch),
    .\output (n2to1_4bits_multiplexer_1_output));
  _2to1_8bits_multiplexer u_2to1_8bits_multiplexer_1 (
    .A(RAM_input), .B(in_4), .selector(run_programming_mode_switch),
    .\output (n2to1_8bits_multiplexer_1_output));
  LED led_22 (.in(Counter_mod_5_output[4]));
  LED led_23 (.in(Counter_mod_5_output[6]));
  LED led_24 (.in(Counter_mod_5_output[5]));
  LED led_25 (.in(Counter_mod_5_output[3]));
  LED led_26 (.in(PC_J));
  LED led_27 (.in(PC_JC));
  and and_1 (and_1_out, clk, RAM_in);
  _2_to_1_Multiplexer u_2_to_1_multiplexer_1 (
    .A(and_1_out), .B(RAM_progamming_push_button_out), .selector(run_programming_mode_switch),
    .\output (n2_to_1_multiplexer_1_output));
  Asynchronous_RAM u_RAM (
    .addresse(n2to1_4bits_multiplexer_1_output), .input_value(n2to1_8bits_multiplexer_1_output),
    .in(n2_to_1_multiplexer_1_output), .out(RAM_out), .controlled_output_value(RAM_output),
    .uncontrolled_output_value(RAM_uncontrolled_output_value));
  LED led_28 (.in(register_8bits_1_uncontrolled_output[3]));
  LED led_29 (.in(register_8bits_1_uncontrolled_output[1]));
  LED led_30 (.in(register_8bits_1_uncontrolled_output[0]));
  LED led_31 (.in(register_8bits_1_uncontrolled_output[2]));
  LED led_32 (.in(Counter_mod_5_output[1]));
  LED led_33 (.in(Counter_mod_5_output[0]));
  LED led_34 (.in(Counter_mod_5_output[2]));
  Bus bus_1 (
    .in_2(RegA_output), .in_3(RegB_output), .in_4(ALU_output), .in_5(RAM_output), .in_6(PC_output),
    .in_7(Inst_reg_output), .to_LEDs(bus_1_to_leds), .out_10(RegA_input), .out_11(RegB_input), .out_12(RAM),
    .out_13(RAM_input), .out_14(PC_input), .out_15(Instr_reg_input), .out_16(Display_input));  // open: in_8, in_9, in_1, out_17
  LED led_35 (.in(bus_1_to_leds[7]));
  LED led_36 (.in(bus_1_to_leds[6]));
  LED led_37 (.in(bus_1_to_leds[5]));
  Button RAM_progamming_push_button (.out(RAM_progamming_push_button_out));
  LED led_38 (.in(RAM_uncontrolled_output_value[7]));
  LED led_39 (.in(RAM_uncontrolled_output_value[4]));
  LED led_40 (.in(RAM_uncontrolled_output_value[6]));
  LED led_41 (.in(RAM_uncontrolled_output_value[5]));
  not not_3 (not_3_out, clk);
  LED interlaced_clock (.in(not_3_out));
  LED led_42 (.in(bus_1_to_leds[2]));
  LED led_43 (.in(bus_1_to_leds[3]));
  LED led_44 (.in(bus_1_to_leds[1]));
  LED led_45 (.in(bus_1_to_leds[4]));
  LED led_46 (.in(RAM_uncontrolled_output_value[2]));
  LED led_47 (.in(RAM_uncontrolled_output_value[0]));
  LED led_48 (.in(RAM_uncontrolled_output_value[1]));
  LED led_49 (.in(RAM_uncontrolled_output_value[3]));
  Counter_mod_5 Counter_mod_5 (.clk(not_3_out), .\output (Counter_mod_5_output[2:0]));
  Decoder_3_to_8 Decoder_3_to_8 (.\input (Counter_mod_5_output[2:0]), .\output (Decoder_3_to_8_output));
  Register_8bits Register (
    .\input (Display_input), .clk(clk), .in_enable(Disp_in),
    .uncontrolled_output(Register_uncontrolled_output));  // open: out_enable, controlled_output
  LED led_50 (.in(Register_uncontrolled_output[7]));
  LED led_51 (.in(bus_1_to_leds[0]));
  LED led_52 (.in(Decoder_3_to_8_output[0]));
  LED led_53 (.in(Decoder_3_to_8_output[1]));
  LED led_54 (.in(Decoder_3_to_8_output[2]));
  LED led_55 (.in(Decoder_3_to_8_output[3]));
  LED led_56 (.in(Decoder_3_to_8_output[4]));
  LED led_57 (.in(Register_uncontrolled_output[5]));
  LED led_58 (.in(Register_uncontrolled_output[4]));
  LED led_59 (.in(Register_uncontrolled_output[3]));
  LED led_60 (.in(Register_uncontrolled_output[6]));
  Pull_Resistor pull_resistor_5 (.node(PC_input[6]));
  Pull_Resistor pull_resistor_6 (.node(PC_input[7]));
  Complement_8_bits Complement (.\input (B), .invert(ALU_sub), .\output (Complement_output));
  LED led_61 (.in(Register_uncontrolled_output[1]));
  LED led_62 (.in(Register_uncontrolled_output[0]));
  LED led_63 (.in(Register_uncontrolled_output[2]));
  Pull_Resistor pull_resistor_7 (.node(PC_input[4]));
  Pull_Resistor pull_resistor_8 (.node(PC_input[5]));
  ROM rom_2 (.addr(Register_uncontrolled_output), .data(rom_2_data));  // open: sel
  ROM rom_3 (.addr(Register_uncontrolled_output), .data(rom_3_data));  // open: sel
  ROM rom_4 (.addr(Register_uncontrolled_output), .data(rom_4_data));  // open: sel
  _7_Segment_Display u_7_segment_display_1 (
    .g(rom_4_data[6]), .f(rom_4_data[5]), .a(rom_4_data[0]), .b(rom_4_data[1]), .e(rom_4_data[4]),
    .d(rom_4_data[3]), .c(rom_4_data[2]));  // open: dp
  and and_2 (and_2_out, clk, PC_J);
  _4_bits_counter Counter (
    .\input (PC_input[3:0]), .clk(clk), .enable(PC_en), .input_enable(and_2_out),
    .\output (Counter_output[3:0]));
  Pull_Resistor pull_resistor_9 (.node(Counter_output[4]));
  LED led_64 (.in(Counter_output[3]));
  LED led_65 (.in(Counter_output[2]));
  LED led_66 (.in(Counter_output[1]));
  Register_8bits register_8bits_2 (
    .\input (RegA_input), .clk(clk), .in_enable(RegA_in), .out_enable(RegA_out),
    .controlled_output(RegA_output), .uncontrolled_output(A));
  adder adder_1 (.A(A), .B(Complement_output), .carry_in(ALU_sub), .carry_out(adder_1_carry_out), .sum(adder_1_sum));
  LED Carry (.in(adder_1_carry_out));
  Register_8bits register_8bits_3 (
    .\input (RegB_input), .clk(clk), .in_enable(RegB_in), .out_enable(1'b0), .controlled_output(RegB_output),
    .uncontrolled_output(B));
  LED led_67 (.in(B[7]));
  Pull_Resistor pull_resistor_10 (.node(Counter_output[7]));
  Pull_Resistor pull_resistor_11 (.node(Counter_output[6]));
  Pull_Resistor pull_resistor_12 (.node(Counter_output[5]));
  LED led_68 (.in(Counter_output[0]));
  LED led_69 (.in(A[4]));
  LED led_70 (.in(A[7]));
  LED led_71 (.in(A[5]));
  LED led_72 (.in(A[6]));
  Tristate_buffer_8_bits tristate_buffer_8_bits_1 (.\input (adder_1_sum), .enable(ALU_out), .\output (ALU_output));
  LED led_73 (.in(adder_1_sum[7]));
  LED led_74 (.in(adder_1_sum[5]));
  LED led_75 (.in(adder_1_sum[6]));
  LED led_76 (.in(adder_1_sum[4]));
  LED led_77 (.in(B[5]));
  LED led_78 (.in(B[3]));
  LED led_79 (.in(B[4]));
  LED led_80 (.in(B[6]));
  _7_Segment_Display u_7_segment_display_2 (
    .g(rom_3_data[6]), .f(rom_3_data[5]), .a(rom_3_data[0]), .b(rom_3_data[1]), .e(rom_3_data[4]),
    .d(rom_3_data[3]), .c(rom_3_data[2]));  // open: dp
  Tristate_buffer_8_bits Buffer (.\input (Counter_output), .enable(PC_out), .\output (PC_output));
  LED led_81 (.in(A[1]));
  LED led_82 (.in(A[2]));
  LED led_83 (.in(A[3]));
  LED led_84 (.in(A[0]));
  LED led_85 (.in(adder_1_sum[0]));
  LED led_86 (.in(adder_1_sum[3]));
  LED led_87 (.in(adder_1_sum[2]));
  LED led_88 (.in(adder_1_sum[1]));
  LED led_89 (.in(B[2]));
  LED led_90 (.in(B[0]));
  LED led_91 (.in(B[1]));
  _7_Segment_Display u_7_segment_display_3 (
    .g(rom_2_data[6]), .f(rom_2_data[5]), .a(rom_2_data[0]), .b(rom_2_data[1]), .e(rom_2_data[4]),
    .d(rom_2_data[3]), .c(rom_2_data[2]));  // open: dp

  // Notes on the sheet:
  //   automatic
  //   Reg
  //   programmable data
  //   inputs switches
  //   Instructions register
  //   Register
  //   Instructions decoder control
  //    signals circuit rom
  //   manual
  //   Clock
  //   programmable address
  //   switches
  //   contents of rom_1 (hex, n*v repeats v):
  //   2002 1018 6*0 2002 1018 22 48 4*0 2002 1018 22 408 140 0 0 0 2002 1018 22 408 340 0 0 0 2002 1018 22
  //   84 4*0 2002 1018 60 5*0 2002 1018 4020 5*0 2002 1018 22 408 340 0 0 0 2002 1018 8020 5*0 2002 1018
  //   6*0 2002 1018 6*0 2002 1018 6*0 2002 1018 6*0 2002 1018 6*0 2002 1018 880 5*0 2002 1018 1
  //   clock signal
  //   Mux
  //   Mux
  //   instruction
  //   Bus
  //   Mux
  //   RAM
  //   address
  //   micro
  //   instruction
  //    Instuctions decoder
  //   Bus
  //   micro
  //   instructions
  //   1
  //   2
  //   3
  //   4
  //   5
  //   Ones ROM
  //   Tens ROM
  //   Hundreds ROM
  //   Register A
  //   Register B
  //   contents of rom_2 (hex, n*v repeats v):
  //   3f 6 5b 4f 66 6d 7d 7 7f 6f 3f 6 5b 4f 66 6d 7d 7 7f 6f 3f 6 5b 4f 66 6d 7d 7 7f 6f 3f 6 5b 4f 66 6d
  //   7d 7 7f 6f 3f 6 5b 4f 66 6d 7d 7 7f 6f 3f 6 5b 4f 66 6d 7d 7 7f 6f 3f 6 5b 4f 66 6d 7d 7 7f 6f 3f 6
  //   5b 4f 66 6d 7d 7 7f 6f 3f 6 5b 4f 66 6d 7d 7 7f 6f 3f 6 5b 4f 66 6d 7d 7 7f 6f 3f 6 5b 4f 66 6d 7d 7
  //   7f 6f 3f 6 5b 4f 66 6d 7d 7 7f 6f 3f 6 5b 4f 66 6d 7d 7 7f 6f 3f 6 5b 4f 66 6d 7d 7 7f 6f 3f 6 5b 4f
  //   66 6d 7d 7 7f 6f 3f 6 5b 4f 66 6d 7d 7 7f 6f 3f 6 5b 4f 66 6d 7d 7 7f 6f 3f 6 5b 4f 66 6d 7d 7 7f 6f
  //   3f 6 5b 4f 66 6d 7d 7 7f 6f 3f 6 5b 4f 66 6d 7d 7 7f 6f 3f 6 5b 4f 66 6d 7d 7 7f 6f 3f 6 5b 4f 66 6d
  //   7d 7 7f 6f 3f 6 5b 4f 66 6d 7d 7 7f 6f 3f 6 5b 4f 66 6d 7d 7 7f 6f 3f 6 5b 4f 66 6d 7d 7 7f 6f 3f 6
  //   5b 4f 66 6d
  //   contents of rom_3 (hex, n*v repeats v):
  //   10*3f 10*6 10*5b 10*4f 10*66 10*6d 10*7d 10*7 10*7f 10*6f 10*3f 10*6 10*5b 10*4f 10*66 10*6d 10*7d
  //   10*7 10*7f 10*6f 10*3f 10*6 10*5b 10*4f 10*66 6*6d
  //   contents of rom_4 (hex, n*v repeats v):
  //   100*3f 100*6 56*5b
  //   Register
  //   ALU
  //   Adder
  //   Register
  //   Display
  //   Buffer
  //   Counter
endmodule
