// Logisim project A register board.circ as structural Verilog: 1 circuit, main circuit A register board
module A_register_board (
);

  wire clk, RegA_in, RegA_out;
  wire [7:0] A, RegA_input, RegA_output;

  Register_8bits register_8bits_1 (
    .\input (RegA_input), .clk(clk), .in_enable(RegA_in), .out_enable(RegA_out),
    .controlled_output(RegA_output), .uncontrolled_output(A));
  LED led_1 (.in(A[5]));
  LED led_2 (.in(A[6]));
  LED led_3 (.in(A[7]));
  LED led_4 (.in(A[1]));
  LED led_5 (.in(A[3]));
  LED led_6 (.in(A[2]));
  LED led_7 (.in(A[4]));
  LED led_8 (.in(A[0]));

  // Notes on the sheet:
  //   Register
endmodule
