// Logisim project ALU board.circ as structural Verilog: 1 circuit, main circuit ALU board
module ALU_board (
);

  wire adder_1_carry_out, ALU_out, ALU_sub;
  wire [7:0] A, adder_1_sum, ALU_output, B, Complement_output;

  Complement_8_bits Complement (.\input (B), .invert(ALU_sub), .\output (Complement_output));
  LED Carry (.in(adder_1_carry_out));
  adder adder_1 (.A(A), .B(Complement_output), .carry_in(ALU_sub), .carry_out(adder_1_carry_out), .sum(adder_1_sum));
  LED led_1 (.in(adder_1_sum[7]));
  Tristate_buffer_8_bits tristate_buffer_8_bits_1 (.\input (adder_1_sum), .enable(ALU_out), .\output (ALU_output));
  LED led_2 (.in(adder_1_sum[3]));
  LED led_3 (.in(adder_1_sum[6]));
  LED led_4 (.in(adder_1_sum[4]));
  LED led_5 (.in(adder_1_sum[5]));
  LED led_6 (.in(adder_1_sum[2]));
  LED led_7 (.in(adder_1_sum[0]));
  LED led_8 (.in(adder_1_sum[1]));

  // Notes on the sheet:
  //   Adder
  //   Buffer
endmodule
