// Logisim project Adder.circ as structural Verilog: 1 circuit, main circuit adder
module adder (
  input  carry_in,
  input  [7:0] A,
  input  [7:0] B,
  output [7:0] sum,
  output carry_out
);

  wire full_adder_1_carry_out, full_adder_2_carry_out, full_adder_3_carry_out, full_adder_4_carry_out,
       full_adder_5_carry_out, full_adder_6_carry_out, full_adder_7_carry_out;

  Full_adder full_adder_1 (.A(A[0]), .B(B[0]), .carry_in(carry_in), .sum(sum[0]), .carry_out(full_adder_1_carry_out));
  Full_adder full_adder_2 (
    .A(A[1]), .B(B[1]), .carry_in(full_adder_1_carry_out), .sum(sum[1]), .carry_out(full_adder_2_carry_out));
  Full_adder full_adder_3 (
    .A(A[2]), .B(B[2]), .carry_in(full_adder_2_carry_out), .sum(sum[2]), .carry_out(full_adder_3_carry_out));
  Full_adder full_adder_4 (
    .A(A[3]), .B(B[3]), .carry_in(full_adder_3_carry_out), .sum(sum[3]), .carry_out(full_adder_4_carry_out));
  Full_adder full_adder_5 (
    .A(A[4]), .B(B[4]), .carry_in(full_adder_4_carry_out), .sum(sum[4]), .carry_out(full_adder_5_carry_out));
  Full_adder full_adder_6 (
    .A(A[5]), .B(B[5]), .carry_in(full_adder_5_carry_out), .sum(sum[5]), .carry_out(full_adder_6_carry_out));
  Full_adder full_adder_7 (
    .A(A[6]), .B(B[6]), .carry_in(full_adder_6_carry_out), .sum(sum[6]), .carry_out(full_adder_7_carry_out));
  Full_adder full_adder_8 (.A(A[7]), .B(B[7]), .carry_in(full_adder_7_carry_out), .sum(sum[7]), .carry_out(carry_out));

  // Notes on the sheet:
  //   full
  //   adder
  //   full
  //   adder
  //   full
  //   adder
  //   full
  //   adder
  //   full
  //   adder
  //   full
  //   adder
  //   full
  //   adder
  //   full
  //   adder
endmodule
