// Logisim project B register board.circ as structural Verilog: 1 circuit, main circuit A register board
module A_register_board (
);

  wire clk, RegB_in, RegB_out;
  wire [7:0] B, RegB_input, RegB_output;

  Register_8bits register_8bits_1 (
    .\input (RegB_input), .clk(clk), .in_enable(RegB_in), .out_enable(RegB_out),
    .controlled_output(RegB_output), .uncontrolled_output(B));
  LED led_1 (.in(B[5]));
  LED led_2 (.in(B[6]));
  LED led_3 (.in(B[7]));
  LED led_4 (.in(B[4]));
  LED led_5 (.in(B[2]));
  LED led_6 (.in(B[1]));
  LED led_7 (.in(B[3]));
  LED led_8 (.in(B[0]));

  // Notes on the sheet:
  //   Register
endmodule
