// Logisim project Buffer8.circ as structural Verilog: 1 circuit, main circuit Tristate buffer 8 bits
module Tristate_buffer_8_bits (
  input  enable,
  input  [7:0] \input ,
  output [7:0] \output 
);

  assign \output [0] = enable ? \input [0] : 1'bz;  // Controlled_Buffer controlled_buffer_1
  assign \output [1] = enable ? \input [1] : 1'bz;  // Controlled_Buffer controlled_buffer_2
  assign \output [2] = enable ? \input [2] : 1'bz;  // Controlled_Buffer controlled_buffer_3
  assign \output [3] = enable ? \input [3] : 1'bz;  // Controlled_Buffer controlled_buffer_4
  assign \output [4] = enable ? \input [4] : 1'bz;  // Controlled_Buffer controlled_buffer_5
  assign \output [5] = enable ? \input [5] : 1'bz;  // Controlled_Buffer controlled_buffer_6
  assign \output [6] = enable ? \input [6] : 1'bz;  // Controlled_Buffer controlled_buffer_7
  assign \output [7] = enable ? \input [7] : 1'bz;  // Controlled_Buffer controlled_buffer_8
endmodule
