// Logisim project Bus board.circ as structural Verilog: 1 circuit, main circuit Bus_board
module Bus_board (
);

  wire [7:0] bus_1_to_leds;

  Bus bus_1 (.to_LEDs(bus_1_to_leds));  // open: in_2, in_3, in_4, in_5, in_6, in_7, in_8, in_9, in_1, out_10, out_11, out_12, out_13, out_14, out_15, out_16, out_17
  LED led_1 (.in(bus_1_to_leds[7]));
  LED led_2 (.in(bus_1_to_leds[5]));
  LED led_3 (.in(bus_1_to_leds[6]));
  LED led_4 (.in(bus_1_to_leds[2]));
  LED led_5 (.in(bus_1_to_leds[3]));
  LED led_6 (.in(bus_1_to_leds[1]));
  LED led_7 (.in(bus_1_to_leds[4]));
  LED led_8 (.in(bus_1_to_leds[0]));

  // Notes on the sheet:
  //   Bus
endmodule
