// Logisim project Bus.circ as structural Verilog: 1 circuit, main circuit Bus
module Bus (
  input  [7:0] in_1,
  input  [7:0] in_2,
  input  [7:0] in_3,
  input  [7:0] in_4,
  input  [7:0] in_5,
  input  [7:0] in_6,
  input  [7:0] in_7,
  input  [7:0] in_8,
  input  [7:0] in_9,
  output [7:0] out_10,
  output [7:0] out_11,
  output [7:0] out_12,
  output [7:0] out_13,
  output [7:0] out_14,
  output [7:0] out_15,
  output [7:0] out_16,
  output [7:0] out_17,
  output [7:0] to_LEDs
);

  Pull_Resistor pull_resistor_1 (.node(in_1[7]));
  Pull_Resistor pull_resistor_2 (.node(in_1[6]));
  Pull_Resistor pull_resistor_3 (.node(in_1[5]));
  Pull_Resistor pull_resistor_4 (.node(in_1[4]));
  Pull_Resistor pull_resistor_5 (.node(in_1[0]));
  Pull_Resistor pull_resistor_6 (.node(in_1[1]));
  Pull_Resistor pull_resistor_7 (.node(in_1[2]));
  Pull_Resistor pull_resistor_8 (.node(in_1[3]));

  assign in_2 = in_1;
  assign in_3 = in_1;
  assign in_4 = in_1;
  assign in_5 = in_1;
  assign in_6 = in_1;
  assign in_7 = in_1;
  assign in_8 = in_1;
  assign in_9 = in_1;
  assign out_10 = in_1;
  assign out_11 = in_1;
  assign out_12 = in_1;
  assign out_13 = in_1;
  assign out_14 = in_1;
  assign out_15 = in_1;
  assign out_16 = in_1;
  assign out_17 = in_1;
  assign to_LEDs = in_1;
endmodule
