// Logisim project Clock board.circ as structural Verilog: 1 circuit, main circuit main
module main (
  input  switch_auto_manual
);

  wire clk, hlt, manual_push_button_out, not_1_out, system_clock_out;

  Clock system_clock (.out(system_clock_out));
  Button manual_push_button (.out(manual_push_button_out));
  LED led_1 (.in(switch_auto_manual));
  LED led_2 (.in(not_1_out));
  not not_1 (not_1_out, switch_auto_manual);
  LED led_3 (.in(clk));
  Clock Clock (
    .clk(system_clock_out), .switch(switch_auto_manual), .manual(manual_push_button_out), .hlt(hlt),
    .clock_output(clk));

  // Notes on the sheet:
  //   halt signal
  //   automatic
  //   manual
  //   clock signal
endmodule
