// Logisim project Clock.circ as structural Verilog: 1 circuit, main circuit Clock
module Clock (
  input  clk,
  input  switch,
  input  manual,
  input  hlt,
  output clock_output
);

  wire and_1_out, and_2_out, not_1_out, not_2_out, or_1_out;

  not not_1 (not_1_out, switch);
  not not_2 (not_2_out, hlt);
  and and_1 (and_1_out, clk, switch);
  and and_2 (and_2_out, not_1_out, manual);
  or or_1 (or_1_out, and_1_out, and_2_out);
  and and_3 (clock_output, or_1_out, not_2_out);

  // Notes on the sheet:
  //   hlt: pull=down
  //   manual: pull=down
endmodule
