// Logisim project Complement.circ as structural Verilog: 1 circuit, main circuit Complement 8 bits
module Complement_8_bits (
  input  invert,
  input  [7:0] \input ,
  output [7:0] \output 
);

  xor xor_1 (\output [0], \input [0], invert);
  xor xor_2 (\output [1], \input [1], invert);
  xor xor_3 (\output [2], \input [2], invert);
  xor xor_4 (\output [3], \input [3], invert);
  xor xor_5 (\output [4], \input [4], invert);
  xor xor_6 (\output [5], \input [5], invert);
  xor xor_7 (\output [6], \input [6], invert);
  xor xor_8 (\output [7], \input [7], invert);
endmodule
