// Logisim project Counter board.circ as structural Verilog: 1 circuit, main circuit Counter board
module Counter_board (
);

  wire clk, PC_en, PC_J, PC_out;
  wire [3:0] Counter_output;
  wire [7:0] PC_input, PC_output;
  wire [7:4] pull_resistor_5_node;

  Pull_Resistor pull_resistor_1 (.node(PC_input[6]));
  Pull_Resistor pull_resistor_2 (.node(PC_input[4]));
  Pull_Resistor pull_resistor_3 (.node(PC_input[5]));
  Pull_Resistor pull_resistor_4 (.node(PC_input[7]));
  _4_bits_counter Counter (
    .\input (PC_input[3:0]), .clk(clk), .enable(PC_en), .input_enable(PC_J), .\output (Counter_output));
  LED led_1 (.in(Counter_output[3]));
  Pull_Resistor pull_resistor_5 (.node(pull_resistor_5_node[4]));
  Pull_Resistor pull_resistor_6 (.node(pull_resistor_5_node[7]));
  Pull_Resistor pull_resistor_7 (.node(pull_resistor_5_node[6]));
  Pull_Resistor pull_resistor_8 (.node(pull_resistor_5_node[5]));
  LED led_2 (.in(Counter_output[1]));
  LED led_3 (.in(Counter_output[0]));
  LED led_4 (.in(Counter_output[2]));
  Tristate_buffer_8_bits Buffer (
    .\input ({pull_resistor_5_node, Counter_output}), .enable(PC_out), .\output (PC_output));
endmodule
