// Logisim project Counter mod 5.circ as structural Verilog: 1 circuit, main circuit Counter mod 5
module Counter_mod_5 (
  input  clk,
  output [2:0] \output 
);

  wire and_1_out, j_k_ff_1_qn, j_k_ff_2_qn, not_1_out;

  J_K_Flip_Flop j_k_ff_1 (
    .J(1'b1), .clk(clk), .K(1'b1), .Q(\output [0]), .Qn(j_k_ff_1_qn), .reset(and_1_out));  // open: preset, en
  J_K_Flip_Flop j_k_ff_2 (
    .J(1'b1), .clk(j_k_ff_1_qn), .K(1'b1), .Q(\output [1]), .Qn(j_k_ff_2_qn), .reset(and_1_out));  // open: preset, en
  J_K_Flip_Flop j_k_ff_3 (
    .J(1'b1), .clk(j_k_ff_2_qn), .K(1'b1), .Q(\output [2]), .reset(and_1_out));  // open: Qn, preset, en
  not not_1 (not_1_out, \output [1]);
  and and_1 (and_1_out, \output [2], not_1_out, \output [0]);
endmodule
