// Logisim project Counter.circ as structural Verilog: 1 circuit, main circuit 4 bits counter
module _4_bits_counter (
  input  clk,
  input  enable,
  input  input_enable,
  input  [3:0] \input ,
  output [3:0] \output 
);

  wire j_k_ff_1_qn, j_k_ff_2_qn, j_k_ff_3_qn;
  wire [7:0] Tristate_Buffer_output;
  wire [7:1] not_1_out;

  not not_1 (not_1_out[1], \input [0]);
  not not_2 (not_1_out[3], \input [1]);
  not not_3 (not_1_out[5], \input [2]);
  not not_4 (not_1_out[7], \input [3]);
  J_K_Flip_Flop j_k_ff_1 (
    .J(1'b1), .clk(clk), .K(1'b1), .Q(\output [0]), .Qn(j_k_ff_1_qn), .preset(Tristate_Buffer_output[0]),
    .en(enable), .reset(Tristate_Buffer_output[1]));
  Tristate_buffer_8_bits Tristate_Buffer (
    .\input ({not_1_out[7], \input [3], not_1_out[5], \input [2], not_1_out[3], \input [1], not_1_out[1], \input [0]}),
    .enable(input_enable), .\output (Tristate_Buffer_output));
  J_K_Flip_Flop j_k_ff_2 (
    .J(1'b1), .clk(j_k_ff_1_qn), .K(1'b1), .Q(\output [1]), .Qn(j_k_ff_2_qn),
    .preset(Tristate_Buffer_output[2]), .en(enable), .reset(Tristate_Buffer_output[3]));
  J_K_Flip_Flop j_k_ff_3 (
    .J(1'b1), .clk(j_k_ff_2_qn), .K(1'b1), .Q(\output [2]), .Qn(j_k_ff_3_qn),
    .preset(Tristate_Buffer_output[4]), .en(enable), .reset(Tristate_Buffer_output[5]));
  J_K_Flip_Flop j_k_ff_4 (
    .J(1'b1), .clk(j_k_ff_3_qn), .K(1'b1), .Q(\output [3]), .preset(Tristate_Buffer_output[6]), .en(enable),
    .reset(Tristate_Buffer_output[7]));  // open: Qn

  // Notes on the sheet:
  //   enable: pull=down
endmodule
