// Logisim project Decoder 3 to 8.circ as structural Verilog: 1 circuit, main circuit Decoder 3 to 8
module Decoder_3_to_8 (
  input  [2:0] \input ,
  output [7:0] \output 
);

  wire not_1_out, not_2_out, not_3_out;

  not not_1 (not_1_out, \input [2]);
  not not_2 (not_2_out, \input [1]);
  not not_3 (not_3_out, \input [0]);
  and and_1 (\output [0], not_3_out, not_2_out, not_1_out);
  and and_2 (\output [1], \input [0], not_2_out, not_1_out);
  and and_3 (\output [2], not_3_out, \input [1], not_1_out);
  and and_4 (\output [3], \input [0], \input [1], not_1_out);
  and and_5 (\output [4], not_3_out, not_2_out, \input [2]);
  and and_6 (\output [5], \input [0], not_2_out, \input [2]);
  and and_7 (\output [6], not_3_out, \input [1], \input [2]);
  and and_8 (\output [7], \input [0], \input [1], \input [2]);
endmodule
