// Logisim project Display board.circ as structural Verilog: 1 circuit, main circuit main
module main (
);

  wire clk, Disp_in;
  wire [7:0] Display_input, Registre_uncontrolled_output, rom_1_data, rom_2_data, rom_3_data;

  Register_8bits Registre (
    .\input (Display_input), .clk(clk), .in_enable(Disp_in),
    .uncontrolled_output(Registre_uncontrolled_output));  // open: out_enable, controlled_output
  LED led_1 (.in(Registre_uncontrolled_output[7]));
  LED led_2 (.in(Registre_uncontrolled_output[6]));
  LED led_3 (.in(Registre_uncontrolled_output[2]));
  LED led_4 (.in(Registre_uncontrolled_output[4]));
  LED led_5 (.in(Registre_uncontrolled_output[5]));
  LED led_6 (.in(Registre_uncontrolled_output[3]));
  LED led_7 (.in(Registre_uncontrolled_output[1]));
  LED led_8 (.in(Registre_uncontrolled_output[0]));
  ROM rom_1 (.addr(Registre_uncontrolled_output), .data(rom_1_data));  // open: sel
  ROM rom_2 (.addr(Registre_uncontrolled_output), .data(rom_2_data));  // open: sel
  ROM rom_3 (.addr(Registre_uncontrolled_output), .data(rom_3_data));  // open: sel
  _7_Segment_Display u_7_segment_display_1 (
    .g(rom_3_data[6]), .f(rom_3_data[5]), .a(rom_3_data[0]), .b(rom_3_data[1]), .e(rom_3_data[4]),
    .d(rom_3_data[3]), .c(rom_3_data[2]));  // open: dp
  _7_Segment_Display u_7_segment_display_2 (
    .g(rom_2_data[6]), .f(rom_2_data[5]), .a(rom_2_data[0]), .b(rom_2_data[1]), .e(rom_2_data[4]),
    .d(rom_2_data[3]), .c(rom_2_data[2]));  // open: dp
  _7_Segment_Display u_7_segment_display_3 (
    .g(rom_1_data[6]), .f(rom_1_data[5]), .a(rom_1_data[0]), .b(rom_1_data[1]), .e(rom_1_data[4]),
    .d(rom_1_data[3]), .c(rom_1_data[2]));  // open: dp

  // Notes on the sheet:
  //   Ones ROM
  //   Tens ROM
  //   Hundreds ROM
  //   contents of rom_1 (hex, n*v repeats v):
  //   3f 6 5b 4f 66 6d 7d 7 7f 6f 3f 6 5b 4f 66 6d 7d 7 7f 6f 3f 6 5b 4f 66 6d 7d 7 7f 6f 3f 6 5b 4f 66 6d
  //   7d 7 7f 6f 3f 6 5b 4f 66 6d 7d 7 7f 6f 3f 6 5b 4f 66 6d 7d 7 7f 6f 3f 6 5b 4f 66 6d 7d 7 7f 6f 3f 6
  //   5b 4f 66 6d 7d 7 7f 6f 3f 6 5b 4f 66 6d 7d 7 7f 6f 3f 6 5b 4f 66 6d 7d 7 7f 6f 3f 6 5b 4f 66 6d 7d 7
  //   7f 6f 3f 6 5b 4f 66 6d 7d 7 7f 6f 3f 6 5b 4f 66 6d 7d 7 7f 6f 3f 6 5b 4f 66 6d 7d 7 7f 6f 3f 6 5b 4f
  //   66 6d 7d 7 7f 6f 3f 6 5b 4f 66 6d 7d 7 7f 6f 3f 6 5b 4f 66 6d 7d 7 7f 6f 3f 6 5b 4f 66 6d 7d 7 7f 6f
  //   3f 6 5b 4f 66 6d 7d 7 7f 6f 3f 6 5b 4f 66 6d 7d 7 7f 6f 3f 6 5b 4f 66 6d 7d 7 7f 6f 3f 6 5b 4f 66 6d
  //   7d 7 7f 6f 3f 6 5b 4f 66 6d 7d 7 7f 6f 3f 6 5b 4f 66 6d 7d 7 7f 6f 3f 6 5b 4f 66 6d 7d 7 7f 6f 3f 6
  //   5b 4f 66 6d
  //   contents of rom_2 (hex, n*v repeats v):
  //   10*3f 10*6 10*5b 10*4f 10*66 10*6d 10*7d 10*7 10*7f 10*6f 10*3f 10*6 10*5b 10*4f 10*66 10*6d 10*7d
  //   10*7 10*7f 10*6f 10*3f 10*6 10*5b 10*4f 10*66 6*6d
  //   contents of rom_3 (hex, n*v repeats v):
  //   100*3f 100*6 56*5b
endmodule
