// Logisim project Full adder.circ as structural Verilog: 1 circuit, main circuit Full adder
module Full_adder (
  input  A,
  input  B,
  input  carry_in,
  output sum,
  output carry_out
);

  wire and_1_out, and_2_out, xor_1_out;

  xor xor_1 (xor_1_out, A, B);
  xor xor_2 (sum, xor_1_out, carry_in);
  and and_1 (and_1_out, carry_in, xor_1_out);
  and and_2 (and_2_out, A, B);
  or or_1 (carry_out, and_1_out, and_2_out);
endmodule
