// Logisim project Instructions register and decoder board.circ as structural Verilog: 1 circuit, main circuit Istructions register and decoder board
module Istructions_register_and_decoder_board (
);

  wire ALU_out, ALU_sub, clk, Disp_in, hlt, Instr_reg_in, Instr_reg_out, not_1_out, PC_en, PC_J, PC_JC,
       PC_out, RAM___in, RAM_in, RAM_out, RegA_in, RegA_out, RegB_in;
  wire [3:0] Inst_reg_output, register_8bits_1_uncontrolled_output;
  wire [6:0] Counter_mod_5_output;
  wire [7:0] Decoder_output, Instr_reg_input;
  wire [7:4] register_8bits_1_controlled_output;

  Register_8bits register_8bits_1 (
    .\input (Instr_reg_input), .clk(clk), .in_enable(Instr_reg_in), .out_enable(Instr_reg_out),
    .controlled_output({register_8bits_1_controlled_output, Inst_reg_output}),
    .uncontrolled_output({Counter_mod_5_output[6:3], register_8bits_1_uncontrolled_output}));
  ROM #(.addrWidth(7), .dataWidth(16)) rom_1 (
    .addr(Counter_mod_5_output),
    .data({PC_JC, PC_J, PC_out, PC_en, Disp_in, RegB_in, ALU_sub, ALU_out, RegA_out, RegA_in, Instr_reg_out, Instr_reg_in, RAM_out, RAM_in, RAM___in, hlt}));  // open: sel
  LED led_1 (.in(RAM_out));
  LED led_2 (.in(hlt));
  LED led_3 (.in(RAM_in));
  LED led_4 (.in(RAM___in));
  LED led_5 (.in(Instr_reg_in));
  LED led_6 (.in(Instr_reg_out));
  LED led_7 (.in(RegA_in));
  LED led_8 (.in(RegA_out));
  LED led_9 (.in(Counter_mod_5_output[6]));
  LED led_10 (.in(Counter_mod_5_output[4]));
  LED led_11 (.in(Counter_mod_5_output[5]));
  LED led_12 (.in(RegB_in));
  LED led_13 (.in(Disp_in));
  LED led_14 (.in(ALU_out));
  LED led_15 (.in(ALU_sub));
  LED led_16 (.in(register_8bits_1_uncontrolled_output[3]));
  LED led_17 (.in(register_8bits_1_uncontrolled_output[1]));
  LED led_18 (.in(register_8bits_1_uncontrolled_output[2]));
  LED led_19 (.in(Counter_mod_5_output[2]));
  LED led_20 (.in(Counter_mod_5_output[1]));
  LED led_21 (.in(Counter_mod_5_output[3]));
  LED led_22 (.in(PC_out));
  LED led_23 (.in(PC_en));
  LED led_24 (.in(PC_J));
  LED led_25 (.in(PC_JC));
  LED interlaced_clock (.in(not_1_out));
  LED led_26 (.in(register_8bits_1_uncontrolled_output[0]));
  LED led_27 (.in(Counter_mod_5_output[0]));
  not not_1 (not_1_out, clk);
  Counter_mod_5 Counter_mod_5 (.clk(not_1_out), .\output (Counter_mod_5_output[2:0]));
  Decoder_3_to_8 Decoder (.\input (Counter_mod_5_output[2:0]), .\output (Decoder_output));
  LED led_28 (.in(Decoder_output[0]));
  LED led_29 (.in(Decoder_output[1]));
  LED led_30 (.in(Decoder_output[2]));
  LED led_31 (.in(Decoder_output[3]));
  LED led_32 (.in(Decoder_output[4]));

  // Notes on the sheet:
  //   Register
  //   Instructions decoder control
  //    signals circuit rom
  //   contents of rom_1 (hex, n*v repeats v):
  //   2002 1018 6*0 2002 1018 22 48 4*0 2002 1018 22 408 140 0 0 0 2002 1018 22 408 340 0 0 0 2002 1018 22
  //   84 4*0 2002 1018 60 5*0 2002 1018 4020 5*0 2002 1018 22 408 340 0 0 0 2002 1018 8020 5*0 2002 1018
  //   6*0 2002 1018 6*0 2002 1018 6*0 2002 1018 6*0 2002 1018 6*0 2002 1018 880 5*0 2002 1018 1
  //   instruction
  //   address
  //   micro
  //   instruction
  //   micro
  //   instruction
  //   1
  //   2
  //   3
  //   4
  //   5
endmodule
