// Logisim project Mux 2-1.circ as structural Verilog: 1 circuit, main circuit 2 to 1 Multiplexer
module _2_to_1_Multiplexer (
  input  selector,
  input  A,
  input  B,
  output \output 
);

  wire and_1_out, and_2_out, not_1_out;

  not not_1 (not_1_out, selector);
  and and_1 (and_1_out, not_1_out, A);
  and and_2 (and_2_out, selector, B);
  or or_1 (\output , and_1_out, and_2_out);
endmodule
