// Logisim project Mux 4bits.circ as structural Verilog: 1 circuit, main circuit 2to1 4bits multiplexer
module _2to1_4bits_multiplexer (
  input  selector,
  input  [3:0] A,
  input  [3:0] B,
  output [3:0] \output 
);

  _2_to_1_Multiplexer u_2_to_1_multiplexer_1 (.A(A[0]), .B(B[0]), .selector(selector), .\output (\output [0]));
  _2_to_1_Multiplexer u_2_to_1_multiplexer_2 (.A(A[1]), .B(B[1]), .selector(selector), .\output (\output [1]));
  _2_to_1_Multiplexer u_2_to_1_multiplexer_3 (.A(A[2]), .B(B[2]), .selector(selector), .\output (\output [2]));
  _2_to_1_Multiplexer u_2_to_1_multiplexer_4 (.A(A[3]), .B(B[3]), .selector(selector), .\output (\output [3]));

  // Notes on the sheet:
  //   Mux
  //   Mux
  //   Mux
  //   Mux
endmodule
