// Logisim project Mux 8bits.circ as structural Verilog: 1 circuit, main circuit 2to1 8bits multiplexer
module _2to1_8bits_multiplexer (
  input  selector,
  input  [7:0] A,
  input  [7:0] B,
  output [7:0] \output 
);

  _2to1_4bits_multiplexer u_2to1_4bits_multiplexer_1 (
    .A(A[3:0]), .B(B[3:0]), .selector(selector), .\output (\output [3:0]));
  _2to1_4bits_multiplexer u_2to1_4bits_multiplexer_2 (
    .A(A[7:4]), .B(B[7:4]), .selector(selector), .\output (\output [7:4]));

  // Notes on the sheet:
  //   Mux
  //   Mux
endmodule
