// Logisim project RAM Board.circ as structural Verilog: 1 circuit, main circuit RAM Board
module RAM_Board (
  input  run_programming_mode_switch,
  input  [3:0] in_2,
  input  [7:0] in_3
);

  wire and_1_out, clk, n2_to_1_multiplexer_1_output, not_1_out, RAM___in, RAM_in, RAM_out,
       RAM_progamming_push_button_out;
  wire [3:0] n2to1_4bits_multiplexer_1_output, n4_bits_register_1_output;
  wire [7:0] asynchronous_ram_1_uncontrolled_output_value, n2to1_8bits_multiplexer_1_output, RAM, RAM_input,
       RAM_output;

  LED led_1 (.in(n4_bits_register_1_output[2]));
  LED led_2 (.in(n4_bits_register_1_output[3]));
  LED led_3 (.in(n4_bits_register_1_output[0]));
  LED led_4 (.in(n4_bits_register_1_output[1]));
  Pull_Resistor pull_resistor_1 (.node(RAM[7]));
  Pull_Resistor pull_resistor_2 (.node(RAM[5]));
  Pull_Resistor pull_resistor_3 (.node(RAM[6]));
  _4_bits_register u_4_bits_register_1 (
    .\input (RAM[3:0]), .clk(clk), .in(RAM___in), .\output (n4_bits_register_1_output));
  Pull_Resistor pull_resistor_4 (.node(RAM[4]));
  LED run_mode_on (.in(not_1_out));
  LED programming_mode_on (.in(run_programming_mode_switch));
  and and_1 (and_1_out, clk, RAM_in);
  not not_1 (not_1_out, run_programming_mode_switch);
  _2to1_4bits_multiplexer u_2to1_4bits_multiplexer_1 (
    .A(n4_bits_register_1_output), .B(in_2), .selector(run_programming_mode_switch),
    .\output (n2to1_4bits_multiplexer_1_output));
  _2to1_8bits_multiplexer u_2to1_8bits_multiplexer_1 (
    .A(RAM_input), .B(in_3), .selector(run_programming_mode_switch),
    .\output (n2to1_8bits_multiplexer_1_output));
  _2_to_1_Multiplexer u_2_to_1_multiplexer_1 (
    .A(and_1_out), .B(RAM_progamming_push_button_out), .selector(run_programming_mode_switch),
    .\output (n2_to_1_multiplexer_1_output));
  Button RAM_progamming_push_button (.out(RAM_progamming_push_button_out));
  Asynchronous_RAM asynchronous_ram_1 (
    .addresse(n2to1_4bits_multiplexer_1_output), .input_value(n2to1_8bits_multiplexer_1_output),
    .in(n2_to_1_multiplexer_1_output), .out(RAM_out), .controlled_output_value(RAM_output),
    .uncontrolled_output_value(asynchronous_ram_1_uncontrolled_output_value));
  LED led_5 (.in(asynchronous_ram_1_uncontrolled_output_value[5]));
  LED led_6 (.in(asynchronous_ram_1_uncontrolled_output_value[7]));
  LED led_7 (.in(asynchronous_ram_1_uncontrolled_output_value[6]));
  LED led_8 (.in(asynchronous_ram_1_uncontrolled_output_value[4]));
  LED led_9 (.in(asynchronous_ram_1_uncontrolled_output_value[2]));
  LED led_10 (.in(asynchronous_ram_1_uncontrolled_output_value[3]));
  LED led_11 (.in(asynchronous_ram_1_uncontrolled_output_value[1]));
  LED led_12 (.in(asynchronous_ram_1_uncontrolled_output_value[0]));

  // Notes on the sheet:
  //   Reg
  //   programmable data
  //   inputs switches
  //   programmable address
  //   switches
  //   Mux
  //   Mux
  //   Mux
  //   RAM
endmodule
