// Logisim project RAM.circ as structural Verilog: 1 circuit, main circuit Asynchronous RAM
module Asynchronous_RAM (
  input  in,
  input  out,
  input  [3:0] addresse,
  input  [7:0] input_value,
  output [7:0] controlled_output_value,
  output [7:0] uncontrolled_output_value
);

  wire and_1_out, and_2_out, nand_1_out, not_1_out, xor_1_out;

  xor xor_1 (xor_1_out, in, out);
  and and_1 (and_1_out, in, xor_1_out);
  and and_2 (and_2_out, xor_1_out, out);
  nand nand_1 (nand_1_out, and_1_out, ~and_2_out);  // NAND_Gate
  not not_1 (not_1_out, nand_1_out);
  RAM #(.addrWidth(4), .bus("asynch")) ram_1 (
    .addr(addresse), .data(uncontrolled_output_value), .sel(1'b1), .ld(nand_1_out), .clr(1'b0));
  Tristate_buffer_8_bits Buffer (.\input (input_value), .enable(not_1_out), .\output (uncontrolled_output_value));
  Tristate_buffer_8_bits Buffer_2 (
    .\input (uncontrolled_output_value), .enable(out), .\output (controlled_output_value));

  // Notes on the sheet:
  //   RAM
endmodule
