// Logisim project Register4.circ as structural Verilog: 1 circuit, main circuit 4 bits register
module _4_bits_register (
  input  clk,
  input  in,
  input  [3:0] \input ,
  output [3:0] \output 
);

  D_Flip_Flop d_ff_1 (.clk(clk), .D(\input [0]), .Q(\output [0]), .en(in));  // open: Qn, preset, reset
  D_Flip_Flop d_ff_2 (.clk(clk), .D(\input [1]), .Q(\output [1]), .en(in));  // open: Qn, preset, reset
  D_Flip_Flop d_ff_3 (.clk(clk), .D(\input [2]), .Q(\output [2]), .en(in));  // open: Qn, preset, reset
  D_Flip_Flop d_ff_4 (.clk(clk), .D(\input [3]), .Q(\output [3]), .en(in));  // open: Qn, preset, reset
endmodule
