// Logisim project Register8.circ as structural Verilog: 1 circuit, main circuit Register 8bits
module Register_8bits (
  input  clk,
  input  in_enable,
  input  out_enable,
  input  [7:0] \input ,
  output [7:0] controlled_output,
  output [7:0] uncontrolled_output
);

  D_Flip_Flop d_ff_1 (
    .clk(clk), .D(\input [0]), .Q(uncontrolled_output[0]), .en(in_enable));  // open: Qn, preset, reset
  D_Flip_Flop d_ff_2 (
    .clk(clk), .D(\input [1]), .Q(uncontrolled_output[1]), .en(in_enable));  // open: Qn, preset, reset
  D_Flip_Flop d_ff_3 (
    .clk(clk), .D(\input [2]), .Q(uncontrolled_output[2]), .en(in_enable));  // open: Qn, preset, reset
  D_Flip_Flop d_ff_4 (
    .clk(clk), .D(\input [3]), .Q(uncontrolled_output[3]), .en(in_enable));  // open: Qn, preset, reset
  D_Flip_Flop d_ff_5 (
    .clk(clk), .D(\input [4]), .Q(uncontrolled_output[4]), .en(in_enable));  // open: Qn, preset, reset
  D_Flip_Flop d_ff_6 (
    .clk(clk), .D(\input [5]), .Q(uncontrolled_output[5]), .en(in_enable));  // open: Qn, preset, reset
  D_Flip_Flop d_ff_7 (
    .clk(clk), .D(\input [6]), .Q(uncontrolled_output[6]), .en(in_enable));  // open: Qn, preset, reset
  D_Flip_Flop d_ff_8 (
    .clk(clk), .D(\input [7]), .Q(uncontrolled_output[7]), .en(in_enable));  // open: Qn, preset, reset
  Tristate_buffer_8_bits tristate_buffer (
    .\input (uncontrolled_output), .enable(out_enable), .\output (controlled_output));
endmodule
